# Fritzing sketch esp_develop_board (saved by Fritzing 0.9.3b)
circuit board: 5cm x 5cm
breadboards: 1

parts:
  U1 = ESP-WROOM-02-AE [part_number=ESP-WROOM-02-AE]
  U2 = Voltage Regulator - 3.3V [package="TO220 [THT]"]
  J1 = female pin header, 9 pins [form="♀ (female)"]
  J2 = female pin header, 9 pins [form="♀ (female)"]
  R1 = Resistor [tolerance=±5% resistance=4.7k package=THT]
  S1 = Toggle Switch [package=THT]
  R2 = Resistor [tolerance=±5% resistance=4.7k package=THT]
  R3 = Resistor [tolerance=±5% resistance=4.7k package=THT]
  R4 = Resistor [tolerance=±5% resistance=4.7k package=THT]
  R5 = Resistor [tolerance=±5% resistance=4.7k package=THT]
  J3 = female pin header, 2 pins [form="♀ (female)"]
  LED1 = LED - 5mm [color="Green (560nm)" package="5 mm [THT]"]
  R6 = Resistor [tolerance=±5% resistance=1k package=THT]
  R7 = Resistor [tolerance=±5% resistance=1k package=THT]
  J5 = female pin header, 2 pins [form="♀ (female)"]
  J6 = female pin header, 2 pins [form="♀ (female)"]
  C1 = Ceramic Capacitor [capacitance=100nF package="100 mil [THT, multilayer]"]
  C2 = Electrolytic Capacitor [capacitance=1µF package="100 mil [THT, electrolytic]"]
  U3 = AE-FT234X [part_number=AE-FT234X]
  S2 = Pushbutton [package="[THT]"]
  LED2 = LED - 5mm [color="Red (633nm)" package="5 mm [THT]"]
  J7 = female pin header, 1 pin [form="♀ (female)"]

nets:
  N1: U1.3V3, U2.output_voltage, J2.pin9, R1.Pin_0, R2.Pin_1, R3.Pin_0, R4.Pin_0, R6.Pin_0, C2.+
  N2: U1.EN, J2.pin8, R1.Pin_1
  N3: U1.IO14, J2.pin7, R7.Pin_1
  N4: U1.IO12, J2.pin6
  N5: U1.IO13, J2.pin5
  N6: U1.IO15, J2.pin4, R5.Pin_1
  N7: U1.IO2, J2.pin3, R4.Pin_1
  N8: U1.IO0, J2.pin2, S1.COM, R3.Pin_1
  GND: U1.GND, U2.GND, J1.pin4, J1.pin9, J2.pin1, S1.L1, R5.Pin_0, LED1.cathode, J6.pin2, C1.1, C2.-, U3.GND, S2.Pin_3, S2.Pin_4, LED2.cathode
  N9: U1.IO16, J1.pin8, J3.pin1
  N10: U1.TOUT, J1.pin7
  N11: U1.RST, J1.pin6, R2.Pin_0, J3.pin2, S2.Pin_1, S2.Pin_2
  N12: U1.IO5, J1.pin5
  N13: U1.TXD, J1.pin3, U3.RxD
  N14: U1.RXD, J1.pin2, U3.TxD
  N15: U1.IO4, J1.pin1
  N16: U2.input_voltage, J6.pin1, C1.0, U3.+5V, J7.pin1
  N17: LED1.anode, R6.Pin_1
  N18: R7.Pin_0, J5.pin2
  N19: J5.pin1, LED2.anode

notes:
  RST
  BT
  DS
  5V
  IO14
  POW
  (c)mmitti 2017
  ESPWR02DEV
  rev2
  HN:mmitti
  TW:@mi_mmitti
  Serial
  ESP 8266

custom parts:
  ESP-WROOM-02-AE: ESP-WROOM-02 with the DIP breakout board by Akizuki-Electronics in Japan. See http://akizukidenshi.com/catalog/g/gK-09758/ for the detauls.
